// Logisim project cap_3_theory_exercises.circ as structural Verilog
module sr_latch (
  input  R,
  input  S,
  output Q,
  output nQ
);

  nor nor_1 (Q, R, nQ);
  nor nor_2 (nQ, Q, S);
endmodule

module d_latch (
  input  D,
  output Q,
  output nQ
);

  wire and_1_out, and_2_out, clock_1_out, not_1_out;

  Clock clock_1 (.out(clock_1_out));
  not not_1 (not_1_out, D);
  and and_1 (and_1_out, clock_1_out, not_1_out);
  and and_2 (and_2_out, clock_1_out, D);
  nor nor_1 (Q, and_1_out, nQ);
  nor nor_2 (nQ, Q, and_2_out);
endmodule

module d_flip_flop (
  input  D,
  output Q,
  output nQ,
  output nQ_2
);

  wire and_1_out, and_2_out, and_3_out, and_4_out, clock_1_out, nor_1_out, not_1_out, not_2_out, not_3_out;

  not not_1 (not_1_out, D);
  and and_1 (and_1_out, not_2_out, not_1_out);
  and and_2 (and_2_out, not_2_out, D);
  not not_2 (not_2_out, clock_1_out);
  nor nor_1 (nor_1_out, and_1_out, nQ);
  nor nor_2 (nQ, nor_1_out, and_2_out);
  Clock clock_1 (.out(clock_1_out));
  not not_3 (not_3_out, nor_1_out);
  and and_3 (and_3_out, clock_1_out, not_3_out);
  and and_4 (and_4_out, clock_1_out, nor_1_out);
  nor nor_3 (Q, and_3_out, nQ_2);
  nor nor_4 (nQ_2, Q, and_4_out);

  // Notes on the sheet:
  //   Master D latch
  //   Slave D latch
endmodule
