// Logisim project d_latch_flip_flop.circ as structural Verilog: 1 circuit, main circuit main
module main (
  input  R,
  input  CLK,
  input  D,
  input  S,
  input  CLK_2,
  input  D_2,
  output Q,
  output out_8,
  output nQ,
  output Q_2,
  output nQ_2
);

  wire and_1_out, and_2_out, not_1_out;

  D_Flip_Flop F1 (.clk(CLK), .D(D), .Q(out_8));  // open: Qn, preset, en, reset
  not not_1 (not_1_out, D_2);
  and and_1 (and_1_out, CLK_2, not_1_out);
  and and_2 (and_2_out, CLK_2, D_2);
  nor nor_1 (Q, R, nQ);
  nor nor_2 (nQ, Q, S);
  nor nor_3 (Q_2, and_1_out, nQ_2);
  nor nor_4 (nQ_2, Q_2, and_2_out);

  // Notes on the sheet:
  //   D latch
  //   SR latch
endmodule
